# Fritzing sketch fritzing (saved by Fritzing 0.9.3b)
circuit board: 1.28616cm x 1.02159cm
breadboards: 1

parts:
  Part1 = Arduino Mega 2560 (Rev3)
  Part2 = Thumb Joystick
  Part3 = Thumb Joystick
  S1 = Toggle Switch [package=THT]
  R1 = Resistor [tolerance=±5% resistance=10k package="1206 [SMD]"]

nets:
  N1: Part1.A0, Part3.HORZ
  N2: Part1.A1, Part3.VERT
  N3: Part1.A2, Part2.HORZ
  N4: Part1.A3, Part2.VERT
  VCC: Part1.5V, Part2.VCC, Part3.VCC, S1.COM
  GND: Part1.GND, Part2.GND, Part3.GND, R1.Pin_0
  N5: Part1.D51, S1.L1, R1.Pin_1
  N6: Part1.D53, Part3.SEL
